// Logisim project 32-bit ALU.circ as structural Verilog: 3 circuits, main circuit 1 bit ALU
module _1_bit_ALU (
  input  Sub,
  input  Cin,
  input  [2:0] in_3,
  input  A,
  input  B,
  input  Less,
  output Result,
  output C_out,
  output out_9
);

  wire and_1_out, nor_1_out, or_1_out, xor_1_out, xor_2_out;

  or or_1 (or_1_out, A, B);
  Adder #(.width(1)) adder_1 (.a(A), .b(xor_1_out), .out(out_9), .cin(Cin), .cout(C_out));
  xor xor_1 (xor_1_out, B, Sub);
  and and_1 (and_1_out, A, B);
  xor xor_2 (xor_2_out, A, B);
  nor nor_1 (nor_1_out, A, B);
  Multiplexer #(.select(3)) multiplexer_1 (
    .in0(and_1_out), .in1(or_1_out), .in2(xor_2_out), .in3(nor_1_out), .in4(out_9), .in5(Less), .out(Result),
    .sel(in_3));  // open: in6, in7, en
endmodule

module _32_Bit_ALU (
  input  Sub,
  input  [2:0] Op,
  input  [31:0] A,
  input  [31:0] B,
  output [31:0] out_5,
  output Zero_flag
);

  wire n1_bit_alu_1_c_out, n1_bit_alu_2_c_out, n1_bit_alu_3_c_out, n1_bit_alu_4_c_out, n1_bit_alu_5_c_out,
       n1_bit_alu_6_c_out, n1_bit_alu_7_c_out, n1_bit_alu_8_c_out, n1_bit_alu_9_c_out, n1_bit_alu_10_c_out,
       n1_bit_alu_11_c_out, n1_bit_alu_12_c_out, n1_bit_alu_13_c_out, n1_bit_alu_14_c_out,
       n1_bit_alu_15_c_out, n1_bit_alu_16_c_out, n1_bit_alu_17_c_out, n1_bit_alu_18_c_out,
       n1_bit_alu_19_c_out, n1_bit_alu_20_c_out, n1_bit_alu_21_c_out, n1_bit_alu_22_c_out,
       n1_bit_alu_23_c_out, n1_bit_alu_24_c_out, n1_bit_alu_25_c_out, n1_bit_alu_26_c_out,
       n1_bit_alu_27_c_out, n1_bit_alu_28_c_out, n1_bit_alu_29_c_out, n1_bit_alu_30_c_out,
       n1_bit_alu_31_c_out, n1_bit_alu_32_out_9;

  _1_bit_ALU u_1_bit_alu_1 (
    .in_3(Op), .A(A[0]), .B(B[0]), .Less(n1_bit_alu_32_out_9), .Result(out_5[0]), .Sub(Sub), .Cin(Sub),
    .C_out(n1_bit_alu_1_c_out));  // open: out_9
  _1_bit_ALU u_1_bit_alu_2 (
    .in_3(Op), .A(A[1]), .B(B[1]), .Less(1'b0), .Result(out_5[1]), .Sub(Sub), .Cin(n1_bit_alu_1_c_out),
    .C_out(n1_bit_alu_2_c_out));  // open: out_9
  _1_bit_ALU u_1_bit_alu_3 (
    .in_3(Op), .A(A[2]), .B(B[2]), .Less(1'b0), .Result(out_5[2]), .Sub(Sub), .Cin(n1_bit_alu_2_c_out),
    .C_out(n1_bit_alu_3_c_out));  // open: out_9
  _1_bit_ALU u_1_bit_alu_4 (
    .in_3(Op), .A(A[3]), .B(B[3]), .Less(1'b0), .Result(out_5[3]), .Sub(Sub), .Cin(n1_bit_alu_3_c_out),
    .C_out(n1_bit_alu_4_c_out));  // open: out_9
  _1_bit_ALU u_1_bit_alu_5 (
    .in_3(Op), .A(A[4]), .B(B[4]), .Less(1'b0), .Result(out_5[4]), .Sub(Sub), .Cin(n1_bit_alu_4_c_out),
    .C_out(n1_bit_alu_5_c_out));  // open: out_9
  _1_bit_ALU u_1_bit_alu_6 (
    .in_3(Op), .A(A[5]), .B(B[5]), .Less(1'b0), .Result(out_5[5]), .Sub(Sub), .Cin(n1_bit_alu_5_c_out),
    .C_out(n1_bit_alu_6_c_out));  // open: out_9
  _1_bit_ALU u_1_bit_alu_7 (
    .in_3(Op), .A(A[6]), .B(B[6]), .Less(1'b0), .Result(out_5[6]), .Sub(Sub), .Cin(n1_bit_alu_6_c_out),
    .C_out(n1_bit_alu_7_c_out));  // open: out_9
  _1_bit_ALU u_1_bit_alu_8 (
    .in_3(Op), .A(A[7]), .B(B[7]), .Less(1'b0), .Result(out_5[7]), .Sub(Sub), .Cin(n1_bit_alu_7_c_out),
    .C_out(n1_bit_alu_8_c_out));  // open: out_9
  _1_bit_ALU u_1_bit_alu_9 (
    .in_3(Op), .A(A[8]), .B(B[8]), .Less(1'b0), .Result(out_5[8]), .Sub(Sub), .Cin(n1_bit_alu_8_c_out),
    .C_out(n1_bit_alu_9_c_out));  // open: out_9
  _1_bit_ALU u_1_bit_alu_10 (
    .in_3(Op), .A(A[9]), .B(B[9]), .Less(1'b0), .Result(out_5[9]), .Sub(Sub), .Cin(n1_bit_alu_9_c_out),
    .C_out(n1_bit_alu_10_c_out));  // open: out_9
  _1_bit_ALU u_1_bit_alu_11 (
    .in_3(Op), .A(A[10]), .B(B[10]), .Less(1'b0), .Result(out_5[10]), .Sub(Sub), .Cin(n1_bit_alu_10_c_out),
    .C_out(n1_bit_alu_11_c_out));  // open: out_9
  _1_bit_ALU u_1_bit_alu_12 (
    .in_3(Op), .A(A[11]), .B(B[11]), .Less(1'b0), .Result(out_5[11]), .Sub(Sub), .Cin(n1_bit_alu_11_c_out),
    .C_out(n1_bit_alu_12_c_out));  // open: out_9
  _1_bit_ALU u_1_bit_alu_13 (
    .in_3(Op), .A(A[12]), .B(B[12]), .Less(1'b0), .Result(out_5[12]), .Sub(Sub), .Cin(n1_bit_alu_12_c_out),
    .C_out(n1_bit_alu_13_c_out));  // open: out_9
  _1_bit_ALU u_1_bit_alu_14 (
    .in_3(Op), .A(A[13]), .B(B[13]), .Less(1'b0), .Result(out_5[13]), .Sub(Sub), .Cin(n1_bit_alu_13_c_out),
    .C_out(n1_bit_alu_14_c_out));  // open: out_9
  _1_bit_ALU u_1_bit_alu_15 (
    .in_3(Op), .A(A[14]), .B(B[14]), .Less(1'b0), .Result(out_5[14]), .Sub(Sub), .Cin(n1_bit_alu_14_c_out),
    .C_out(n1_bit_alu_15_c_out));  // open: out_9
  _1_bit_ALU u_1_bit_alu_16 (
    .in_3(Op), .A(A[15]), .B(B[15]), .Less(1'b0), .Result(out_5[15]), .Sub(Sub), .Cin(n1_bit_alu_15_c_out),
    .C_out(n1_bit_alu_16_c_out));  // open: out_9
  _1_bit_ALU u_1_bit_alu_17 (
    .in_3(Op), .A(A[16]), .B(B[16]), .Less(1'b0), .Result(out_5[16]), .Sub(Sub), .Cin(n1_bit_alu_16_c_out),
    .C_out(n1_bit_alu_17_c_out));  // open: out_9
  _1_bit_ALU u_1_bit_alu_18 (
    .in_3(Op), .A(A[17]), .B(B[17]), .Less(1'b0), .Result(out_5[17]), .Sub(Sub), .Cin(n1_bit_alu_17_c_out),
    .C_out(n1_bit_alu_18_c_out));  // open: out_9
  _1_bit_ALU u_1_bit_alu_19 (
    .in_3(Op), .A(A[18]), .B(B[18]), .Less(1'b0), .Result(out_5[18]), .Sub(Sub), .Cin(n1_bit_alu_18_c_out),
    .C_out(n1_bit_alu_19_c_out));  // open: out_9
  _1_bit_ALU u_1_bit_alu_20 (
    .in_3(Op), .A(A[19]), .B(B[19]), .Less(1'b0), .Result(out_5[19]), .Sub(Sub), .Cin(n1_bit_alu_19_c_out),
    .C_out(n1_bit_alu_20_c_out));  // open: out_9
  _1_bit_ALU u_1_bit_alu_21 (
    .in_3(Op), .A(A[20]), .B(B[20]), .Less(1'b0), .Result(out_5[20]), .Sub(Sub), .Cin(n1_bit_alu_20_c_out),
    .C_out(n1_bit_alu_21_c_out));  // open: out_9
  _1_bit_ALU u_1_bit_alu_22 (
    .in_3(Op), .A(A[21]), .B(B[21]), .Less(1'b0), .Result(out_5[21]), .Sub(Sub), .Cin(n1_bit_alu_21_c_out),
    .C_out(n1_bit_alu_22_c_out));  // open: out_9
  _1_bit_ALU u_1_bit_alu_23 (
    .in_3(Op), .A(A[22]), .B(B[22]), .Less(1'b0), .Result(out_5[22]), .Sub(Sub), .Cin(n1_bit_alu_22_c_out),
    .C_out(n1_bit_alu_23_c_out));  // open: out_9
  _1_bit_ALU u_1_bit_alu_24 (
    .in_3(Op), .A(A[23]), .B(B[23]), .Less(1'b0), .Result(out_5[23]), .Sub(Sub), .Cin(n1_bit_alu_23_c_out),
    .C_out(n1_bit_alu_24_c_out));  // open: out_9
  _1_bit_ALU u_1_bit_alu_25 (
    .in_3(Op), .A(A[24]), .B(B[24]), .Less(1'b0), .Result(out_5[24]), .Sub(Sub), .Cin(n1_bit_alu_24_c_out),
    .C_out(n1_bit_alu_25_c_out));  // open: out_9
  _1_bit_ALU u_1_bit_alu_26 (
    .in_3(Op), .A(A[25]), .B(B[25]), .Less(1'b0), .Result(out_5[25]), .Sub(Sub), .Cin(n1_bit_alu_25_c_out),
    .C_out(n1_bit_alu_26_c_out));  // open: out_9
  _1_bit_ALU u_1_bit_alu_27 (
    .in_3(Op), .A(A[26]), .B(B[26]), .Less(1'b0), .Result(out_5[26]), .Sub(Sub), .Cin(n1_bit_alu_26_c_out),
    .C_out(n1_bit_alu_27_c_out));  // open: out_9
  _1_bit_ALU u_1_bit_alu_28 (
    .in_3(Op), .A(A[27]), .B(B[27]), .Less(1'b0), .Result(out_5[27]), .Sub(Sub), .Cin(n1_bit_alu_27_c_out),
    .C_out(n1_bit_alu_28_c_out));  // open: out_9
  _1_bit_ALU u_1_bit_alu_29 (
    .in_3(Op), .A(A[28]), .B(B[28]), .Less(1'b0), .Result(out_5[28]), .Sub(Sub), .Cin(n1_bit_alu_28_c_out),
    .C_out(n1_bit_alu_29_c_out));  // open: out_9
  _1_bit_ALU u_1_bit_alu_30 (
    .in_3(Op), .A(A[29]), .B(B[29]), .Less(1'b0), .Result(out_5[29]), .Sub(Sub), .Cin(n1_bit_alu_29_c_out),
    .C_out(n1_bit_alu_30_c_out));  // open: out_9
  _1_bit_ALU u_1_bit_alu_31 (
    .in_3(Op), .A(A[30]), .B(B[30]), .Less(1'b0), .Result(out_5[30]), .Sub(Sub), .Cin(n1_bit_alu_30_c_out),
    .C_out(n1_bit_alu_31_c_out));  // open: out_9
  _1_bit_ALU u_1_bit_alu_32 (
    .in_3(Op), .A(A[31]), .B(B[31]), .Less(1'b0), .Result(out_5[31]), .Sub(Sub), .Cin(n1_bit_alu_31_c_out),
    .out_9(n1_bit_alu_32_out_9));  // open: C_out
  nor nor_1 (Zero_flag, out_5[0], out_5[1], out_5[2], out_5[3], out_5[4], out_5[5], out_5[6], out_5[7], out_5[8], out_5[9], out_5[10], out_5[11], out_5[12], out_5[13], out_5[14], out_5[15], out_5[16], out_5[17], out_5[18], out_5[19], out_5[20], out_5[21], out_5[22], out_5[23], out_5[24], out_5[25], out_5[26], out_5[27], out_5[28], out_5[29], out_5[30], out_5[31]);
endmodule

module SingleCycleCPU (
  input  in_1,
  input  [2:0] in_2,
  input  [31:0] in_3,
  input  [31:0] in_4,
  output [31:0] out_5,
  output out_6
);

  _32_Bit_ALU u_32_bit_alu_1 (.A(in_3), .B(in_4), .out_5(out_5), .Zero_flag(out_6), .Sub(in_1), .Op(in_2));
endmodule
