// Logisim project 8-bit ALU.circ as structural Verilog: 2 circuits, main circuit main
module main (
  input  Cin,
  input  Sub,
  input  [2:0] Operation,
  input  A,
  input  B,
  input  Less,
  output Result,
  output Cout,
  output Set
);

  wire and_1_out, not_1_out, not_2_out, not_3_out, or_1_out, xor_1_out, xor_2_out;

  xor xor_1 (xor_1_out, B, Sub);
  and and_1 (and_1_out, A, B);
  or or_1 (or_1_out, A, B);
  xor xor_2 (xor_2_out, A, B);
  Adder #(.width(1)) adder_1 (.a(A), .b(xor_1_out), .out(Set), .cin(Cin), .cout(Cout));
  not not_1 (not_1_out, xor_2_out);
  not not_2 (not_2_out, and_1_out);
  not not_3 (not_3_out, or_1_out);
  Multiplexer #(.select(3), .enable("false")) multiplexer_1 (
    .in0(and_1_out), .in1(or_1_out), .in2(xor_2_out), .in3(not_1_out), .in4(not_2_out), .in5(not_3_out),
    .in6(Set), .in7(Less), .out(Result), .sel(Operation));

  // Notes on the sheet:
  //   1Bit ALU
  //   0 - AND
  //   1- OR
  //   2 - XOR
  //   3 - XNOR
  //   4 - NAND
  //   5 - NOR
  //   6 - ADD/SUB
  //   7 - LESS THAN
endmodule

module _8_bit_ALU (
  input  [7:0] A,
  input  Sub,
  input  [2:0] Op,
  input  [7:0] B,
  output [7:0] Result,
  output Zero
);

  wire main_1_cout, main_2_cout, main_3_cout, main_4_cout, main_5_cout, main_6_cout, main_7_cout, main_8_set;

  main main_1 (
    .A(A[0]), .B(B[0]), .Less(main_8_set), .Result(Result[0]), .Cin(Sub), .Sub(Sub), .Operation(Op),
    .Cout(main_1_cout));  // open: Set
  main main_2 (
    .A(A[1]), .B(B[1]), .Less(1'b0), .Result(Result[1]), .Cin(main_1_cout), .Sub(Sub), .Operation(Op),
    .Cout(main_2_cout));  // open: Set
  main main_3 (
    .A(A[2]), .B(B[2]), .Less(1'b0), .Result(Result[2]), .Cin(main_2_cout), .Sub(Sub), .Operation(Op),
    .Cout(main_3_cout));  // open: Set
  main main_4 (
    .A(A[3]), .B(B[3]), .Less(1'b0), .Result(Result[3]), .Cin(main_3_cout), .Sub(Sub), .Operation(Op),
    .Cout(main_4_cout));  // open: Set
  main main_5 (
    .A(A[4]), .B(B[4]), .Less(1'b0), .Result(Result[4]), .Cin(main_4_cout), .Sub(Sub), .Operation(Op),
    .Cout(main_5_cout));  // open: Set
  main main_6 (
    .A(A[5]), .B(B[5]), .Less(1'b0), .Result(Result[5]), .Cin(main_5_cout), .Sub(Sub), .Operation(Op),
    .Cout(main_6_cout));  // open: Set
  main main_7 (
    .A(A[6]), .B(B[6]), .Less(1'b0), .Result(Result[6]), .Cin(main_6_cout), .Sub(Sub), .Operation(Op),
    .Cout(main_7_cout));  // open: Set
  main main_8 (
    .A(A[7]), .B(B[7]), .Less(1'b0), .Result(Result[7]), .Cin(main_7_cout), .Sub(Sub), .Operation(Op),
    .Set(main_8_set));  // open: Cout
  nor nor_1 (Zero, Result[0], Result[1], Result[2], Result[3], Result[4], Result[5], Result[6], Result[7]);
endmodule
