// Logisim project ALU.circ as structural Verilog
module ALU (
  input  [3:0] Number_A,
  input  [3:0] Number_B,
  input  [3:0] Control,
  output C_out,
  output [3:0] Output
);

  wire n4_bit_alu_1_a__b, n4_bit_alu_1_a_b, n4_bit_alu_1_a_b_2;

  _4_bit_ALU u_4_bit_alu_1 (
    .Number_A(Number_A), .Number_B(Number_B), .out_4(C_out), .out_5(Output), .in_3(Control),
    .A_B(n4_bit_alu_1_a_b), .A__B(n4_bit_alu_1_a__b), .A_B_2(n4_bit_alu_1_a_b_2));
  LED A_B (.in(n4_bit_alu_1_a_b));
  LED A__B (.in(n4_bit_alu_1_a__b));
  LED A_B_2 (.in(n4_bit_alu_1_a_b_2));

  // Notes on the sheet:
  //   0000- Addition
  //   0001- Subtraction
  //   1000 - AND
  //   1001 - OR
  //   1010 - XOR
  //   1011 - XNOR
  //   1100 - NAND
  //   1101 - NOR
  //   1110 - NOT-A
  //   1111- NOR-B
endmodule

module half_adder (
  input  B,
  input  A,
  output S,
  output C
);

  xor xor_1 (S, B, A);
  and and_1 (C, B, A);
endmodule

module full_adder (
  input  A,
  input  B,
  input  C_in,
  output Sum,
  output C_out
);

  wire half_adder_1_c, half_adder_1_s, half_adder_2_c;

  half_adder half_adder_1 (.B(B), .A(A), .S(half_adder_1_s), .C(half_adder_1_c));
  half_adder half_adder_2 (.B(C_in), .A(half_adder_1_s), .S(Sum), .C(half_adder_2_c));
  or or_1 (C_out, half_adder_1_c, half_adder_2_c);
endmodule

// 4-bitAdder
module _4_bit_Adde_Subtractor (
  input  M,
  input  [3:0] Number_A,
  input  [3:0] Number_B,
  output [3:0] Out,
  output C4
);

  wire full_adder_2_c_out, full_adder_3_c_out, full_adder_4_c_out, xor_1_out, xor_2_out, xor_3_out, xor_4_out;

  xor xor_1 (xor_1_out, M, Number_B[3]);
  full_adder full_adder_1 (.Sum(Out[3]), .C_out(C4), .A(xor_1_out), .B(Number_A[3]), .C_in(full_adder_2_c_out));
  xor xor_2 (xor_2_out, M, Number_B[2]);
  full_adder full_adder_2 (
    .Sum(Out[2]), .C_out(full_adder_2_c_out), .A(xor_2_out), .B(Number_A[2]), .C_in(full_adder_3_c_out));
  xor xor_3 (xor_3_out, M, Number_B[1]);
  full_adder full_adder_3 (
    .Sum(Out[1]), .C_out(full_adder_3_c_out), .A(xor_3_out), .B(Number_A[1]), .C_in(full_adder_4_c_out));
  xor xor_4 (xor_4_out, M, Number_B[0]);
  full_adder full_adder_4 (.Sum(Out[0]), .C_out(full_adder_4_c_out), .A(xor_4_out), .B(Number_A[0]), .C_in(M));
endmodule

module _8_bit_Adder_subtracter (
  input  [7:0] Number_A,
  input  M,
  input  [7:0] NNumber_B,
  output [7:0] Out,
  output C4
);

  wire full_adder_2_c_out, full_adder_3_c_out, full_adder_4_c_out, full_adder_5_c_out, full_adder_6_c_out,
       full_adder_7_c_out, full_adder_8_c_out, xor_1_out, xor_2_out, xor_3_out, xor_4_out, xor_5_out,
       xor_6_out, xor_7_out, xor_8_out;

  xor xor_1 (xor_1_out, M, NNumber_B[7]);
  full_adder full_adder_1 (.Sum(Out[7]), .C_out(C4), .A(xor_1_out), .B(Number_A[7]), .C_in(full_adder_2_c_out));
  xor xor_2 (xor_2_out, M, NNumber_B[6]);
  full_adder full_adder_2 (
    .Sum(Out[6]), .C_out(full_adder_2_c_out), .A(xor_2_out), .B(Number_A[6]), .C_in(full_adder_3_c_out));
  xor xor_3 (xor_3_out, M, NNumber_B[5]);
  full_adder full_adder_3 (
    .Sum(Out[5]), .C_out(full_adder_3_c_out), .A(xor_3_out), .B(Number_A[5]), .C_in(full_adder_4_c_out));
  xor xor_4 (xor_4_out, NNumber_B[4], M);
  full_adder full_adder_4 (
    .Sum(Out[4]), .C_out(full_adder_4_c_out), .A(xor_4_out), .B(Number_A[4]), .C_in(full_adder_5_c_out));
  xor xor_5 (xor_5_out, M, NNumber_B[3]);
  full_adder full_adder_5 (
    .Sum(Out[3]), .C_out(full_adder_5_c_out), .A(xor_5_out), .B(Number_A[3]), .C_in(full_adder_6_c_out));
  xor xor_6 (xor_6_out, M, NNumber_B[2]);
  full_adder full_adder_6 (
    .Sum(Out[2]), .C_out(full_adder_6_c_out), .A(xor_6_out), .B(Number_A[2]), .C_in(full_adder_7_c_out));
  full_adder full_adder_7 (
    .Sum(Out[1]), .C_out(full_adder_7_c_out), .A(xor_7_out), .B(Number_A[1]), .C_in(full_adder_8_c_out));
  xor xor_7 (xor_7_out, M, NNumber_B[1]);
  full_adder full_adder_8 (.Sum(Out[0]), .C_out(full_adder_8_c_out), .A(xor_8_out), .B(Number_A[0]), .C_in(M));
  xor xor_8 (xor_8_out, M, NNumber_B[0]);
endmodule

// Comparator
module _8_bit_Comparator (
  input  [7:0] A,
  input  [7:0] B,
  output A_B,
  output A__B,
  output A_B_2
);

  wire and_2_out, and_3_out, n4_bit_comparator_1_a__b, n4_bit_comparator_1_a_b, n4_bit_comparator_1_a_b_2,
       n4_bit_comparator_2_a__b, n4_bit_comparator_2_a_b, n4_bit_comparator_2_a_b_2;

  _4_bit_Comparator u_4_bit_comparator_1 (
    .B(B[3:0]), .A(A[3:0]), .A_B(n4_bit_comparator_1_a_b), .A__B(n4_bit_comparator_1_a__b),
    .A_B_2(n4_bit_comparator_1_a_b_2));
  _4_bit_Comparator u_4_bit_comparator_2 (
    .B(B[7:4]), .A(A[7:4]), .A_B(n4_bit_comparator_2_a_b), .A__B(n4_bit_comparator_2_a__b),
    .A_B_2(n4_bit_comparator_2_a_b_2));
  and and_1 (A__B, n4_bit_comparator_1_a__b, n4_bit_comparator_2_a__b);
  and and_2 (and_2_out, n4_bit_comparator_1_a_b, n4_bit_comparator_2_a__b);
  and and_3 (and_3_out, n4_bit_comparator_2_a__b, n4_bit_comparator_1_a_b_2);
  or or_1 (A_B, and_2_out, n4_bit_comparator_2_a_b);
  or or_2 (A_B_2, and_3_out, n4_bit_comparator_2_a_b_2);
endmodule

module _4_bit_Comparator (
  input  [3:0] B,
  input  [3:0] A,
  output A_B,
  output A__B,
  output A_B_2
);

  wire and_1_out, and_2_out, and_3_out, and_4_out, and_5_out, and_6_out, and_7_out, and_8_out, not_1_out,
       not_2_out, not_3_out, not_4_out, not_5_out, not_6_out, not_7_out, not_8_out, xnor_1_out, xnor_2_out,
       xnor_3_out, xnor_4_out;

  not not_1 (not_1_out, A[1]);
  not not_2 (not_2_out, A[2]);
  not not_3 (not_3_out, A[0]);
  not not_4 (not_4_out, A[3]);
  not not_5 (not_5_out, B[1]);
  not not_6 (not_6_out, B[3]);
  not not_7 (not_7_out, B[2]);
  not not_8 (not_8_out, B[0]);
  xnor xnor_1 (xnor_1_out, A[3], B[3]);
  xnor xnor_2 (xnor_2_out, A[2], B[2]);
  xnor xnor_3 (xnor_3_out, A[1], B[1]);
  xnor xnor_4 (xnor_4_out, A[0], B[0]);
  and and_1 (and_1_out, A[3], not_6_out);
  and and_2 (and_2_out, xnor_1_out, not_7_out, A[2]);
  and and_3 (and_3_out, xnor_1_out, xnor_2_out, not_5_out, A[1]);
  and and_4 (and_4_out, xnor_1_out, A[0], not_8_out, xnor_2_out, xnor_3_out);
  and and_5 (and_5_out, B[3], not_4_out);
  and and_6 (and_6_out, B[2], not_2_out, xnor_1_out);
  and and_7 (and_7_out, B[1], xnor_2_out, not_1_out, xnor_1_out);
  and and_8 (and_8_out, xnor_3_out, B[0], not_3_out, xnor_2_out, xnor_1_out);
  or or_1 (A_B, and_1_out, and_2_out, and_3_out, and_4_out);
  and and_9 (A__B, xnor_1_out, xnor_2_out, xnor_3_out, xnor_4_out);
  or or_2 (A_B_2, and_5_out, and_6_out, and_7_out, and_8_out);
endmodule

module _4_bit_ALU (
  input  [3:0] Number_A,
  input  [3:0] Number_B,
  input  [3:0] in_3,
  output out_4,
  output [3:0] out_5,
  output A_B,
  output A__B,
  output A_B_2
);

  wire [3:0] gates_1_and, gates_1_nand, gates_1_nor, gates_1_not_a, gates_1_not_b, gates_1_or, gates_1_xnor,
       gates_1_xor, n4_bit_adde_subtractor_1_out;

  _4_bit_Adde_Subtractor u_4_bit_adde_subtractor_1 (
    .C4(out_4), .M(in_3[0]), .Number_A(Number_A), .Number_B(Number_B), .Out(n4_bit_adde_subtractor_1_out));
  _4_bit_Comparator u_4_bit_comparator_1 (.B(Number_B), .A(Number_A), .A_B(A_B), .A__B(A__B), .A_B_2(A_B_2));
  gates gates_1 (
    .A(Number_A), .B(Number_B), .AND(gates_1_and), .OR(gates_1_or), .XOR(gates_1_xor), .XNOR(gates_1_xnor),
    .NAND(gates_1_nand), .NOR(gates_1_nor), .NOT_A(gates_1_not_a), .NOT_B(gates_1_not_b));
  Multiplexer #(.select(4), .width(4), .enable("false")) multiplexer_1 (
    .in0(n4_bit_adde_subtractor_1_out), .in1(n4_bit_adde_subtractor_1_out), .in8(gates_1_and),
    .in9(gates_1_or), .in10(gates_1_xor), .in11(gates_1_xnor), .in12(gates_1_nand), .in13(gates_1_nor),
    .in14(gates_1_not_a), .in15(gates_1_not_b), .out(out_5), .sel(in_3));  // open: in2, in3, in4, in5, in6, in7
endmodule

module gates (
  input  [3:0] A,
  input  [3:0] B,
  output [3:0] AND,
  output [3:0] OR,
  output [3:0] XOR,
  output [3:0] XNOR,
  output [3:0] NAND,
  output [3:0] NOR,
  output [3:0] NOT_A,
  output [3:0] NOT_B
);

  assign AND = A & B;  // AND_Gate and_1, 4 bits wide
  assign OR = A | B;  // OR_Gate or_1, 4 bits wide
  assign NOT_A = ~A;  // NOT_Gate not_1, 4 bits wide
  assign NOT_B = ~B;  // NOT_Gate not_2, 4 bits wide
  assign XOR = A ^ B;  // XOR_Gate xor_1, 4 bits wide
  assign XNOR = ~(A ^ B);  // XNOR_Gate xnor_1, 4 bits wide
  assign NAND = ~(A & B);  // NAND_Gate nand_1, 4 bits wide
  assign NOR = ~(A | B);  // NOR_Gate nor_1, 4 bits wide

  // Notes on the sheet:
  //   1000 - AND
  //   1001 - OR
  //   1010 - XOR
  //   1011 - XNOR
  //   1100 - NAND
  //   1101 - NOR
  //   1110 - NOT-A
  //   1111- NOR-B
endmodule

module gates_8 (
  input  [7:0] A,
  input  [7:0] B,
  output [7:0] AND,
  output [7:0] OR,
  output [7:0] XOR,
  output [7:0] XNOR,
  output [7:0] NAND,
  output [7:0] NOR,
  output [7:0] NOT_A,
  output [7:0] NOT_B
);

  assign AND = A & B;  // AND_Gate and_1, 8 bits wide
  assign OR = A | B;  // OR_Gate or_1, 8 bits wide
  assign NOT_A = ~A;  // NOT_Gate not_1, 8 bits wide
  assign NOT_B = ~B;  // NOT_Gate not_2, 8 bits wide
  assign XOR = A ^ B;  // XOR_Gate xor_1, 8 bits wide
  assign XNOR = ~(A ^ B);  // XNOR_Gate xnor_1, 8 bits wide
  assign NAND = ~(A & B);  // NAND_Gate nand_1, 8 bits wide
  assign NOR = ~(A | B);  // NOR_Gate nor_1, 8 bits wide

  // Notes on the sheet:
  //   1000 - AND
  //   1001 - OR
  //   1010 - XOR
  //   1011 - XNOR
  //   1100 - NAND
  //   1101 - NOR
  //   1110 - NOT-A
  //   1111- NOR-B
endmodule

module _8_bit_ALU (
  input  [7:0] Number_A,
  input  [7:0] Number_B,
  input  [3:0] in_3,
  output C_out,
  output [7:0] Output,
  output A_B,
  output A__B,
  output A_B_2
);

  wire [7:0] gates_8_1_and, gates_8_1_nand, gates_8_1_nor, gates_8_1_not_a, gates_8_1_not_b, gates_8_1_or,
       gates_8_1_xnor, gates_8_1_xor, n8_bit_adder_subtracter_1_out;

  _8_bit_Adder_subtracter u_8_bit_adder_subtracter_1 (
    .C4(C_out), .Number_A(Number_A), .M(in_3[0]), .NNumber_B(Number_B), .Out(n8_bit_adder_subtracter_1_out));
  _8_bit_Comparator u_8_bit_comparator_1 (.A(Number_A), .B(Number_B), .A_B(A_B), .A__B(A__B), .A_B_2(A_B_2));
  gates_8 gates_8_1 (
    .A(Number_A), .B(Number_B), .AND(gates_8_1_and), .OR(gates_8_1_or), .XOR(gates_8_1_xor),
    .XNOR(gates_8_1_xnor), .NAND(gates_8_1_nand), .NOR(gates_8_1_nor), .NOT_A(gates_8_1_not_a),
    .NOT_B(gates_8_1_not_b));
  Multiplexer #(.select(4), .width(8), .enable("false")) multiplexer_1 (
    .in0(n8_bit_adder_subtracter_1_out), .in1(n8_bit_adder_subtracter_1_out), .in8(gates_8_1_and),
    .in9(gates_8_1_or), .in10(gates_8_1_xor), .in11(gates_8_1_xnor), .in12(gates_8_1_nand),
    .in13(gates_8_1_nor), .in14(gates_8_1_not_a), .in15(gates_8_1_not_b), .out(Output), .sel(in_3));  // open: in2, in3, in4, in5, in6, in7

  // Notes on the sheet:
  //   0000- Addition
  //   0001- Subtraction
  //   1000 - AND
  //   1001 - OR
  //   1010 - XOR
  //   1011 - XNOR
  //   1100 - NAND
  //   1101 - NOR
  //   1110 - NOT-A
  //   1111- NOR-B
endmodule

module ALU_2 (
  input  [7:0] Number_A,
  input  [7:0] Number_B,
  input  [3:0] Control,
  output C_out,
  output [7:0] Output
);

  wire n8_bit_alu_1_a__b, n8_bit_alu_1_a_b, n8_bit_alu_1_a_b_2;

  _8_bit_ALU u_8_bit_alu_1 (
    .Number_A(Number_A), .Number_B(Number_B), .C_out(C_out), .Output(Output), .A__B(n8_bit_alu_1_a__b),
    .in_3(Control), .A_B(n8_bit_alu_1_a_b), .A_B_2(n8_bit_alu_1_a_b_2));
  LED A_B (.in(n8_bit_alu_1_a_b));
  LED A__B (.in(n8_bit_alu_1_a__b));
  LED A_B_2 (.in(n8_bit_alu_1_a_b_2));

  // Notes on the sheet:
  //   0000- Addition
  //   0001- Subtraction
  //   1000 - AND
  //   1001 - OR
  //   1010 - XOR
  //   1011 - XNOR
  //   1100 - NAND
  //   1101 - NOR
  //   1110 - NOT-A
  //   1111- NOR-B
endmodule
